# Fritzing sketch 24LC1025 (saved by Fritzing 0.7.11b)
breadboards: 1

parts:
  Arduino1 = Arduino
  IC1 = 24LC1025 [package=THT]

nets:
  N1: Arduino1.GND, IC1.A0, IC1.A1, IC1.0V, IC1.WP_-_Write_Protect
  N2: Arduino1.+5V, IC1.A2_(CS), IC1.+V
  N3: Arduino1.SCL, IC1.SCL_-_I2C_Clock
  N4: Arduino1.SDA, IC1.SDA_-_I2C_Data
