# Fritzing sketch mcp_eeprom (saved by Fritzing 0.7.11b)
breadboards: 1

parts:
  Arduino1 = Arduino
  IC1 = 24LC01 [package=THT]
  T1 = LM35 Temperature Sensor [thermistor_type=NTC package="TO92 [THT]"]

nets:
  GND: Arduino1.GND, IC1.0V, IC1.WP_-_Write_Protect, T1.GND
  N1: Arduino1.+5V, IC1.A2, IC1.+V, T1.+Vs
  N2: Arduino1.A0, T1.Vout
  N3: Arduino1.SCL, IC1.SCL_-_I2C_Clock
  N4: Arduino1.SDA, IC1.SDA_-_I2C_Data
